// Logisim project brianiac.circ as structural Verilog: 7 circuits, main circuit main
module main (
  input  in_1,
  input  in_2,
  input  in_3
);

  wire and_1_out, and_2_out, and_3_out, and_4_out, and_5_out, and_6_out, and_8_out, and_9_out, and_10_out,
       and_11_out, and_12_out, clock_1_out, clock_2_out, clock_3_out, clock_4_out, clock_5_out,
       decoder_1_out0, decoder_2_out0, decoder_2_out1, decoder_2_out2, decoder_2_out3, decoder_2_out4,
       decoder_2_out5, decoder_2_out6, decoder_2_out7, HWR, IO, keyboard_1_avail, LWR, not_1_out, or_1_out,
       RW;
  wire [2:0] cpu_1_addr_2, cpu_1_addr_3;
  wire [6:0] controlled_buffer_1_out, cpu_1_dataout, keyboard_1_data;
  wire [7:0] bit_extender_1_out, bit_extender_2_out, controlled_buffer_2_out, controlled_buffer_3_out,
       ram_1_dout, ram_2_dout, rom_1_data, rom_2_data;
  wire [12:0] cpu_1_addr;
  wire [15:7] cpu_1_dataout_2;

  Decoder #(.select(3)) decoder_1 (
    .out0(decoder_1_out0), .sel(cpu_1_addr_2), .en(IO));  // open: out1, out2, out3, out4, out5, out6, out7
  // Probe on {controlled_buffer_2_out, controlled_buffer_3_out}
  not not_1 (not_1_out, HWR);
  and and_1 (and_1_out, RW, decoder_1_out0);
  and and_2 (and_2_out, ~RW, decoder_1_out0);  // AND_Gate
  Clock clock_1 (.out(clock_1_out));
  Keyboard #(.trigger("falling")) keyboard_1 (
    .clk(clock_1_out), .re(and_3_out), .clr(in_2), .avail(keyboard_1_avail), .data(keyboard_1_data));
  and and_3 (and_3_out, HWR, and_1_out);
  and and_4 (and_4_out, and_1_out, not_1_out);
  and and_5 (and_5_out, and_2_out, ~LWR);  // AND_Gate
  Clock clock_2 (.out(clock_2_out));
  assign controlled_buffer_1_out = and_5_out ? cpu_1_dataout : 7'bz;  // Controlled_Buffer controlled_buffer_1
  Clock clock_3 (.out(clock_3_out));
  TTY tty_1 (.data(controlled_buffer_1_out), .clk(clock_3_out), .we(and_5_out), .clr(in_3));
  assign bit_extender_1_out = {{7{1'b0}}, keyboard_1_avail};  // Bit_Extender bit_extender_1
  assign controlled_buffer_2_out = and_4_out ? bit_extender_1_out : 8'bz;  // Controlled_Buffer controlled_buffer_2
  // Probe on {controlled_buffer_2_out, controlled_buffer_3_out}
  assign bit_extender_2_out = {{1{1'b0}}, keyboard_1_data};  // Bit_Extender bit_extender_2
  assign controlled_buffer_3_out = and_3_out ? bit_extender_2_out : 8'bz;  // Controlled_Buffer controlled_buffer_3
  CPU cpu_1 (
    .CLK(clock_2_out), .DATAin({controlled_buffer_2_out, controlled_buffer_3_out}), .RESET(in_1),
    .readwrite(RW), .ADDR({cpu_1_addr_3, cpu_1_addr[12], cpu_1_addr_2, cpu_1_addr[8:0]}),
    .DATAout({cpu_1_dataout_2, cpu_1_dataout}), .HWR(HWR), .LWR(LWR));
  Decoder #(.select(3)) decoder_2 (
    .out0(decoder_2_out0), .out1(decoder_2_out1), .out2(decoder_2_out2), .out3(decoder_2_out3),
    .out4(decoder_2_out4), .out5(decoder_2_out5), .out6(decoder_2_out6), .out7(decoder_2_out7),
    .sel(cpu_1_addr_3), .en(1'b1));
  // Probe on {cpu_1_addr_3, cpu_1_addr[12], cpu_1_addr_2, cpu_1_addr[8:0]}
  // Probe on {cpu_1_dataout_2, cpu_1_dataout}
  and and_6 (and_6_out, decoder_2_out7, ~cpu_1_addr[12]);  // AND_Gate
  and and_7 (IO, decoder_2_out7, cpu_1_addr[12]);
  and and_8 (and_8_out, RW, decoder_2_out0);
  or or_1 (or_1_out, decoder_2_out1, decoder_2_out2, decoder_2_out3, decoder_2_out4, decoder_2_out5, decoder_2_out6, and_6_out);
  and and_9 (and_9_out, ~RW, or_1_out);  // AND_Gate
  and and_10 (and_10_out, or_1_out, RW);
  ROM #(.addrWidth(12)) rom_1 (.addr({cpu_1_addr[12], cpu_1_addr_2, cpu_1_addr[8:1]}), .data(rom_1_data));
  Clock clock_4 (.out(clock_4_out));
  and and_11 (and_11_out, ~HWR, and_9_out);  // AND_Gate
  and and_12 (and_12_out, and_9_out, ~LWR);  // AND_Gate
  RAM #(.addrWidth(15), .asyncread("true")) ram_1 (
    .addr({cpu_1_addr_3, cpu_1_addr[12], cpu_1_addr_2, cpu_1_addr[8:1]}), .we(and_11_out), .oe(and_10_out),
    .clk(clock_4_out), .din(cpu_1_dataout_2[15:8]), .dout(ram_1_dout));
  assign controlled_buffer_2_out = and_8_out ? rom_1_data : 8'bz;  // Controlled_Buffer controlled_buffer_4
  assign controlled_buffer_2_out = and_10_out ? ram_1_dout : 8'bz;  // Controlled_Buffer controlled_buffer_5
  ROM #(.addrWidth(12)) rom_2 (.addr({cpu_1_addr[12], cpu_1_addr_2, cpu_1_addr[8:1]}), .data(rom_2_data));
  Clock clock_5 (.out(clock_5_out));
  RAM #(.addrWidth(15), .asyncread("true")) ram_2 (
    .addr({cpu_1_addr_3, cpu_1_addr[12], cpu_1_addr_2, cpu_1_addr[8:1]}), .we(and_12_out), .oe(and_10_out),
    .clk(clock_5_out), .din({cpu_1_dataout_2[7], cpu_1_dataout}), .dout(ram_2_dout));
  assign controlled_buffer_3_out = and_8_out ? rom_2_data : 8'bz;  // Controlled_Buffer controlled_buffer_6
  assign controlled_buffer_3_out = and_10_out ? ram_2_dout : 8'bz;  // Controlled_Buffer controlled_buffer_7

  // Notes on the sheet:
  //   contents of rom_1 (hex, n*v repeats v):
  //   63 f0 63 0 5d 0 5d 0 5d 0 5d 0 41 0 71 f0 31 0 45 0 5e 71 f0 5e 75 f0 31 0 45 0 63 0 75 f0 5e 24 23
  //   0 64 70 31 0 43 0 5d 0 24 21 0 41 0 60 24 21 0 5e 43 55 44 6d d
  //   contents of rom_2 (hex, n*v repeats v):
  //   e0 0 10 70 f0 46 f0 1c f0 2a f0 30 0 c 0 0 0 1 0 1c f 0 1 f 0 1 0 d 0 44 0 a 0 1 f 0 e0 2 ef 1 0 0 0
  //   66 f0 30 0 10 1 0 4e fe 0 e0 2 f 50 20 65 6f
endmodule

module PC (
  input  [15:0] PCin,
  input  CLK,
  input  PCset,
  input  RESET,
  input  PCen,
  output [15:0] PCout
);

  wire or_1_out;
  wire [15:0] adder_1_out, multiplexer_1_out;

  Adder #(.width(16)) adder_1 (.a(PCout), .b(16'h2), .out(adder_1_out));  // open: cin, cout
  Multiplexer #(.width(16)) multiplexer_1 (.in0(adder_1_out), .in1(PCin), .out(multiplexer_1_out), .sel(PCset));
  or or_1 (or_1_out, PCset, PCen);
  Register #(.width(16)) register_1 (.D(multiplexer_1_out), .en(or_1_out), .clk(CLK), .Q(PCout), .clr(RESET));
endmodule

module RegisterFile (
  input  [3:0] ASEL,
  input  [3:0] BSEL,
  input  [15:0] Din,
  input  WE,
  input  [3:0] WSEL,
  input  CLK,
  input  RESET,
  output [15:0] Aout,
  output [15:0] Bout
);

  wire demultiplexer_1_out0, demultiplexer_1_out1, demultiplexer_1_out2, demultiplexer_1_out3,
       demultiplexer_1_out4, demultiplexer_1_out5, demultiplexer_1_out6, demultiplexer_1_out7,
       demultiplexer_1_out8, demultiplexer_1_out9, demultiplexer_1_out10, demultiplexer_1_out11,
       demultiplexer_1_out12, demultiplexer_1_out13, demultiplexer_1_out14, demultiplexer_1_out15;
  wire [15:0] R0_q, R1_q, R2_q, R3_q, R4_q, R5_q, R6_q, R7_q, R8_q, R9_q, R10_q, R11_q, R12_q, R13_q, R14_q,
       R15_q;

  Demultiplexer #(.select(4)) demultiplexer_1 (
    .out0(demultiplexer_1_out0), .out1(demultiplexer_1_out1), .out2(demultiplexer_1_out2),
    .out3(demultiplexer_1_out3), .out4(demultiplexer_1_out4), .out5(demultiplexer_1_out5),
    .out6(demultiplexer_1_out6), .out7(demultiplexer_1_out7), .out8(demultiplexer_1_out8),
    .out9(demultiplexer_1_out9), .out10(demultiplexer_1_out10), .out11(demultiplexer_1_out11),
    .out12(demultiplexer_1_out12), .out13(demultiplexer_1_out13), .out14(demultiplexer_1_out14),
    .out15(demultiplexer_1_out15), .in(WE), .sel(WSEL));
  Register #(.trigger("falling"), .width(16)) R0 (.D(Din), .en(demultiplexer_1_out0), .clk(CLK), .Q(R0_q), .clr(RESET));
  Register #(.trigger("falling"), .width(16)) R1 (.D(Din), .en(demultiplexer_1_out1), .clk(CLK), .Q(R1_q), .clr(RESET));
  Register #(.trigger("falling"), .width(16)) R2 (.D(Din), .en(demultiplexer_1_out2), .clk(CLK), .Q(R2_q), .clr(RESET));
  Register #(.trigger("falling"), .width(16)) R3 (.D(Din), .en(demultiplexer_1_out3), .clk(CLK), .Q(R3_q), .clr(RESET));
  Register #(.trigger("falling"), .width(16)) R4 (.D(Din), .en(demultiplexer_1_out4), .clk(CLK), .Q(R4_q), .clr(RESET));
  Register #(.trigger("falling"), .width(16)) R5 (.D(Din), .en(demultiplexer_1_out5), .clk(CLK), .Q(R5_q), .clr(RESET));
  Register #(.trigger("falling"), .width(16)) R6 (.D(Din), .en(demultiplexer_1_out6), .clk(CLK), .Q(R6_q), .clr(RESET));
  Register #(.trigger("falling"), .width(16)) R7 (.D(Din), .en(demultiplexer_1_out7), .clk(CLK), .Q(R7_q), .clr(RESET));
  Register #(.trigger("falling"), .width(16)) R8 (.D(Din), .en(demultiplexer_1_out8), .clk(CLK), .Q(R8_q), .clr(RESET));
  Register #(.trigger("falling"), .width(16)) R9 (.D(Din), .en(demultiplexer_1_out9), .clk(CLK), .Q(R9_q), .clr(RESET));
  Register #(.trigger("falling"), .width(16)) R10 (
    .D(Din), .en(demultiplexer_1_out10), .clk(CLK), .Q(R10_q), .clr(RESET));
  Register #(.trigger("falling"), .width(16)) R11 (
    .D(Din), .en(demultiplexer_1_out11), .clk(CLK), .Q(R11_q), .clr(RESET));
  Register #(.trigger("falling"), .width(16)) R12 (
    .D(Din), .en(demultiplexer_1_out12), .clk(CLK), .Q(R12_q), .clr(RESET));
  Register #(.trigger("falling"), .width(16)) R13 (
    .D(Din), .en(demultiplexer_1_out13), .clk(CLK), .Q(R13_q), .clr(RESET));
  Register #(.trigger("falling"), .width(16)) R14 (
    .D(Din), .en(demultiplexer_1_out14), .clk(CLK), .Q(R14_q), .clr(RESET));
  Register #(.trigger("falling"), .width(16)) R15 (
    .D(Din), .en(demultiplexer_1_out15), .clk(CLK), .Q(R15_q), .clr(RESET));
  Multiplexer #(.select(4), .width(16)) multiplexer_1 (
    .in0(R0_q), .in1(R1_q), .in2(R2_q), .in3(R3_q), .in4(R4_q), .in5(R5_q), .in6(R6_q), .in7(R7_q),
    .in8(R8_q), .in9(R9_q), .in10(R10_q), .in11(R11_q), .in12(R12_q), .in13(R13_q), .in14(R14_q),
    .in15(R15_q), .out(Aout), .sel(ASEL));
  Multiplexer #(.select(4), .width(16)) multiplexer_2 (
    .in0(R0_q), .in1(R1_q), .in2(R2_q), .in3(R3_q), .in4(R4_q), .in5(R5_q), .in6(R6_q), .in7(R7_q),
    .in8(R8_q), .in9(R9_q), .in10(R10_q), .in11(R11_q), .in12(R12_q), .in13(R13_q), .in14(R14_q),
    .in15(R15_q), .out(Bout), .sel(BSEL));
endmodule

module ALU (
  input  Cin,
  input  [15:0] Rn,
  input  [15:0] Rm,
  input  [3:0] ALUop,
  output C,
  output Z,
  output N,
  output [15:0] Rout,
  output V
);

  wire adder_1_cout, and_1_out, and_3_out, comparator_1_eq, subtractor_1_bout, xnor_1_out, xor_2_out;
  wire [15:0] adder_1_out, and_2_out, not_1_out, or_1_out, shifter_1_out, shifter_2_out, subtractor_1_out,
       xor_1_out;

  and and_1 (and_1_out, Cin, ~comparator_1_eq);  // AND_Gate
  Adder #(.width(16)) adder_1 (.a(Rn), .b(Rm), .out(adder_1_out), .cin(and_1_out), .cout(adder_1_cout));
  Subtractor #(.width(16)) subtractor_1 (
    .a(Rn), .b(Rm), .out(subtractor_1_out), .bin(and_1_out), .bout(subtractor_1_bout));
  assign and_2_out = Rn & Rm;  // AND_Gate and_2, 16 bits wide
  assign or_1_out = Rn | Rm;  // OR_Gate or_1, 16 bits wide
  assign not_1_out = ~Rn;  // NOT_Gate not_1, 16 bits wide
  Shifter #(.shift("lr"), .width(16)) shifter_1 (.in(Rn), .\dist (4'b0001), .out(shifter_1_out));
  Shifter #(.width(16)) shifter_2 (.in(Rn), .\dist (4'b0001), .out(shifter_2_out));
  assign xor_1_out = Rn ^ Rm;  // XOR_Gate xor_1, 16 bits wide
  Multiplexer #(.select(4)) multiplexer_1 (
    .in0(adder_1_cout), .in1(subtractor_1_bout), .in2(1'b0), .in3(1'b0), .in4(1'b0), .in5(1'b0), .in6(1'b0),
    .in7(1'b0), .in8(subtractor_1_bout), .in9(1'b0), .in10(1'b0), .in11(1'b0), .in12(1'b0), .in13(1'b0),
    .in14(1'b0), .in15(1'b0), .out(C), .sel(ALUop));
  Multiplexer #(.select(4), .width(16)) multiplexer_2 (
    .in0(adder_1_out), .in1(subtractor_1_out), .in2(and_2_out), .in3(or_1_out), .in4(xor_1_out),
    .in5(not_1_out), .in6(shifter_1_out), .in7(shifter_2_out), .in8(subtractor_1_out), .in9(and_2_out),
    .in10({16{1'b0}}), .in11({16{1'b0}}), .in12({16{1'b0}}), .in13({16{1'b0}}), .in14({16{1'b0}}),
    .in15({16{1'b0}}), .out({N, Rout[14:0]}), .sel(ALUop));
  xor xor_2 (xor_2_out, N, Rm[15]);
  xnor xnor_1 (xnor_1_out, Rm[15], Rn[15]);
  Comparator #(.mode("unsigned"), .width(4)) comparator_1 (
    .a(ALUop), .b(4'b1000), .eq(comparator_1_eq));  // open: gt, lt
  nor nor_1 (Z, Rout[0], Rout[1], Rout[2], Rout[3], Rout[4], Rout[5], Rout[6], Rout[7], Rout[8], Rout[9], Rout[10], Rout[11], Rout[12], Rout[13], Rout[14], N);
  and and_3 (and_3_out, xor_2_out, xnor_1_out);
  Multiplexer #(.select(4)) multiplexer_3 (
    .in0(and_3_out), .in1(and_3_out), .in2(1'b0), .in3(1'b0), .in4(1'b0), .in5(1'b0), .in6(1'b0), .in7(1'b0),
    .in8(and_3_out), .in9(1'b0), .in10(1'b0), .in11(1'b0), .in12(1'b0), .in13(1'b0), .in14(1'b0),
    .in15(1'b0), .out(V), .sel(ALUop));

  assign Rout[15] = N;
endmodule

module Control (
  input  RESET,
  input  CLK,
  input  [15:0] IRin,
  input  [15:0] STATUS,
  output [3:0] REGsel,
  output [3:0] Rnsel,
  output [3:0] Rmsel,
  output [3:0] ALUop,
  output RMsrc,
  output STload,
  output IRload,
  output PCen,
  output [1:0] REGsrc,
  output IMMload,
  output PCsrc,
  output PCload,
  output DOUTenable,
  output ByteEn,
  output [1:0] ADDRsel,
  output PCsave,
  output REGWrite,
  output DATAOUTsrc
);

  wire alugrp, and_1_out, and_2_out, and_3_out, and_4_out, and_5_out, and_6_out, and_7_out, and_8_out,
       and_9_out, bnc, bnz, bra, branchgrp, brc, brz, call, cp, ld, ldstgrp, miscgrp, mov, or_1_out,
       or_2_out, or_3_out, or_4_out, ret, st, test;
  wire [1:0] multiplexer_9_out, multiplexer_12_out, tstate;

  or or_1 (or_1_out, st, ld);
  Multiplexer #(.select(2)) multiplexer_1 (.in0(1'b1), .in1(1'b0), .in2(1'b0), .in3(1'b0), .out(IRload), .sel(tstate));
  Multiplexer #(.select(2)) multiplexer_2 (.in0(1'b1), .in1(IRin[8]), .in2(1'b0), .in3(1'b0), .out(PCen), .sel(tstate));
  Multiplexer #(.select(2)) multiplexer_3 (
    .in0(1'b0), .in1(IRin[8]), .in2(1'b0), .in3(1'b0), .out(IMMload), .sel(tstate));
  and and_1 (and_1_out, IRin[12], or_1_out);
  and and_2 (and_2_out, IRin[8], st);
  Counter #(.max('h3), .width(2)) counter_1 (.clr(RESET), .clk(CLK), .Q(tstate));  // open: load, up, count, D, carry
  Multiplexer #(.select(2)) multiplexer_4 (
    .in0(1'b0), .in1(1'b0), .in2(and_1_out), .in3(and_1_out), .out(ByteEn), .sel(tstate));
  Multiplexer #(.select(2)) multiplexer_5 (
    .in0(1'b0), .in1(1'b0), .in2(and_2_out), .in3(and_2_out), .out(DATAOUTsrc), .sel(tstate));
  Multiplexer #(.select(2)) multiplexer_6 (
    .in0(1'b0), .in1(1'b0), .in2(1'b0), .in3(alugrp), .out(STload), .sel(tstate));
  and and_3 (and_3_out, brc, STATUS[0]);
  and and_4 (and_4_out, brz, STATUS[1]);
  and and_5 (and_5_out, bnz, ~STATUS[1]);  // AND_Gate
  and and_6 (and_6_out, bnc, ~STATUS[0]);  // AND_Gate
  Multiplexer #(.select(2)) multiplexer_7 (.in0(1'b0), .in1(1'b0), .in2(1'b0), .in3(call), .out(PCsave), .sel(tstate));
  or or_2 (or_2_out, call, bra, and_4_out, and_5_out, and_3_out, and_6_out, ret);
  Multiplexer #(.select(2)) multiplexer_8 (
    .in0(1'b0), .in1(1'b0), .in2(1'b0), .in3(or_2_out), .out(PCload), .sel(tstate));
  Multiplexer #(.select(4), .width(2)) multiplexer_9 (
    .in0(2'b00), .in1(2'b00), .in2(2'b11), .in3(2'b11), .in4(2'b10), .in5(2'b10), .in6(2'b00), .in7(2'b00),
    .in8(2'b00), .in9(2'b01), .in10(2'b00), .in11(2'b00), .in12(2'b00), .in13(2'b00), .in14(2'b00),
    .in15(2'b00), .out(multiplexer_9_out), .sel({mov, ld, alugrp, IRin[8]}));
  and and_7 (and_7_out, IRin[8], alugrp);
  Multiplexer #(.select(2)) multiplexer_10 (
    .in0(1'b0), .in1(1'b0), .in2(and_7_out), .in3(and_7_out), .out(RMsrc), .sel(tstate));
  Multiplexer #(.select(2), .width(2)) multiplexer_11 (
    .in0(2'b00), .in1(2'b00), .in2(2'b00), .in3(multiplexer_9_out), .out(REGsrc), .sel(tstate));
  Multiplexer #(.select(3), .width(2)) multiplexer_12 (
    .in0(2'b00), .in1(2'b00), .in2(2'b01), .in3(2'b11), .in4(2'b10), .in5(2'b11), .in6(2'b00), .in7(2'b00),
    .out(multiplexer_12_out), .sel({ld, st, IRin[8]}));
  Multiplexer #(.select(2), .width(2)) multiplexer_13 (
    .in0(2'b00), .in1(2'b00), .in2(multiplexer_12_out), .in3(2'b00), .out(ADDRsel), .sel(tstate));
  Decoder #(.select(4)) decoder_1 (
    .out0(bra), .out1(brz), .out2(bnz), .out3(brc), .out4(bnc), .out14(call), .out15(ret), .sel(IRin[12:9]),
    .en(branchgrp));  // open: out5, out6, out7, out8, out9, out10, out11, out12, out13
  and and_8 (and_8_out, branchgrp, IRin[8]);
  Multiplexer #(.select(2)) multiplexer_14 (
    .in0(1'b0), .in1(1'b0), .in2(1'b0), .in3(and_8_out), .out(PCsrc), .sel(tstate));
  or or_3 (or_3_out, cp, test);
  and and_9 (and_9_out, ~or_3_out, alugrp);  // AND_Gate
  Decoder #(.select(3)) decoder_2 (
    .out0(miscgrp), .out1(alugrp), .out2(branchgrp), .out3(ldstgrp), .sel(IRin[15:13]));  // open: out4, out5, out6, out7, en
  or or_4 (or_4_out, and_9_out, ld, mov, call);
  Decoder #(.select(2)) decoder_3 (.out0(ld), .out1(mov), .out2(st), .sel(IRin[10:9]), .en(ldstgrp));  // open: out3
  Decoder #(.select(4)) decoder_4 (
    .out8(cp), .out9(test), .sel(IRin[12:9]), .en(alugrp));  // open: out0, out1, out2, out3, out4, out5, out6, out7, out10, out11, out12, out13, out14, out15
  Multiplexer #(.select(2)) multiplexer_15 (
    .in0(1'b0), .in1(1'b0), .in2(st), .in3(1'b0), .out(DOUTenable), .sel(tstate));
  Multiplexer #(.select(2)) multiplexer_16 (
    .in0(1'b0), .in1(1'b0), .in2(1'b0), .in3(or_4_out), .out(REGWrite), .sel(tstate));

  assign ALUop = IRin[12:9];
  assign REGsel = IRin[7:4];
  assign Rmsel = IRin[3:0];
  assign Rnsel = IRin[7:4];

  // Other names for the same wires on the sheet: func[3:0] = IRin[12:9]; irbit8 = IRin[8]; op[2:0] = IRin[15:13];
  //   Rm[3:0] = IRin[3:0]; Rn[3:0] = IRin[7:4]; C = STATUS[0]; Z = STATUS[1]; N = STATUS[2]; V = STATUS[3]
endmodule

module CPU (
  input  CLK,
  input  [15:0] DATAin,
  input  RESET,
  output readwrite,
  output [15:0] ADDR,
  output [15:0] DATAout,
  output HWR,
  output LWR
);

  wire byteen, doutsrc, imload, irload, outen, pcen, pcload, pcsave, pcsrc, rmsrc, rwr, stload;
  wire [1:0] addrsel, regsrc;
  wire [3:0] alu_1_c, aluop, regsel, rmsel, rnsel;
  wire [15:0] alu_1_rout, databus_1_dout, IMR_q, IR_q, multiplexer_1_out, multiplexer_2_out,
       multiplexer_3_out, multiplexer_4_out, multiplexer_5_out, multiplexer_6_out, pc_1_pcout,
       registerfile_1_aout, registerfile_1_bout, STR_q;

  Multiplexer #(.width(16)) multiplexer_1 (
    .in0(registerfile_1_bout), .in1(registerfile_1_bout), .out(multiplexer_1_out), .sel(doutsrc));
  DataBus databus_1 (
    .dataIn(DATAin), .din(multiplexer_1_out), .wr(outen), .ByteEn(byteen), .A0(ADDR[0]),
    .dout(databus_1_dout), .dataOut(DATAout), .HWR(HWR), .LWR(LWR));
  Multiplexer #(.disabled("Z"), .width(16)) multiplexer_2 (
    .in0(registerfile_1_bout), .in1(pc_1_pcout), .out(multiplexer_2_out), .sel(pcsave));
  Multiplexer #(.select(2), .width(16)) multiplexer_3 (
    .in0(multiplexer_2_out), .in1(IMR_q), .in2(databus_1_dout), .in3(alu_1_rout), .out(multiplexer_3_out),
    .sel(regsrc));
  Register #(.trigger("falling"), .width(16)) MAR (
    .D(multiplexer_4_out), .clk(CLK), .Q(ADDR), .clr(RESET));  // open: en
  not not_1 (readwrite, outen);
  Multiplexer #(.select(2), .width(16)) multiplexer_4 (
    .in0(pc_1_pcout), .in1(registerfile_1_aout), .in2(registerfile_1_bout), .in3(IMR_q),
    .out(multiplexer_4_out), .sel(addrsel));
  Register #(.width(16)) IR (.D(databus_1_dout), .en(irload), .clk(CLK), .Q(IR_q), .clr(RESET));
  RegisterFile registerfile_1 (
    .ASEL(rnsel), .BSEL(rmsel), .Din(multiplexer_3_out), .WE(rwr), .WSEL(regsel), .CLK(CLK), .RESET(RESET),
    .Aout(registerfile_1_aout), .Bout(registerfile_1_bout));
  Control control_1 (
    .RESET(RESET), .CLK(CLK), .IRin(IR_q), .STATUS(STR_q), .REGsel(regsel), .Rnsel(rnsel), .Rmsel(rmsel),
    .ALUop(aluop), .RMsrc(rmsrc), .STload(stload), .IRload(irload), .PCen(pcen), .REGsrc(regsrc),
    .IMMload(imload), .PCsrc(pcsrc), .PCload(pcload), .DOUTenable(outen), .ByteEn(byteen), .ADDRsel(addrsel),
    .PCsave(pcsave), .REGWrite(rwr), .DATAOUTsrc(doutsrc));
  Register #(.width(16)) IMR (.D(databus_1_dout), .en(imload), .clk(CLK), .Q(IMR_q), .clr(RESET));
  Multiplexer #(.width(16)) multiplexer_5 (
    .in0(registerfile_1_bout), .in1(IMR_q), .out(multiplexer_5_out), .sel(pcsrc));
  Multiplexer #(.width(16)) multiplexer_6 (
    .in0(registerfile_1_bout), .in1(IMR_q), .out(multiplexer_6_out), .sel(rmsrc));
  PC pc_1 (.PCin(multiplexer_5_out), .CLK(CLK), .PCset(pcload), .RESET(RESET), .PCen(pcen), .PCout(pc_1_pcout));
  ALU alu_1 (
    .Cin(STR_q[0]), .Rn(registerfile_1_aout), .Rm(multiplexer_6_out), .ALUop(aluop), .C(alu_1_c[0]),
    .Z(alu_1_c[1]), .N(alu_1_c[2]), .Rout(alu_1_rout), .V(alu_1_c[3]));
  Register #(.width(16)) STR (.D({{12{1'b0}}, alu_1_c}), .en(stload), .clk(CLK), .Q(STR_q), .clr(RESET));

  // Other names for the same wires on the sheet: A0 = ADDR[0]
endmodule

module DataBus (
  input  [15:0] dataIn,
  input  [15:0] din,
  input  wr,
  input  ByteEn,
  input  A0,
  output [15:0] dout,
  output [15:0] dataOut,
  output HWR,
  output LWR
);

  wire not_1_out;
  wire [15:0] and_1_out, shifter_1_out, shifter_2_out;

  assign and_1_out = dataIn & 16'hff;  // AND_Gate and_1, 16 bits wide
  Shifter #(.shift("lr"), .width(16)) shifter_1 (.in(dataIn), .\dist (4'b1000), .out(shifter_1_out));
  Shifter #(.width(16)) shifter_2 (.in(din), .\dist (4'b1000), .out(shifter_2_out));
  Multiplexer multiplexer_1 (.in0(1'b0), .in1(A0), .out(HWR), .sel(ByteEn));
  Multiplexer #(.disabled("Z"), .enable("true"), .select(2), .width(16)) multiplexer_2 (
    .in0(din), .in1(din), .in2(shifter_2_out), .out(dataOut), .sel({LWR, HWR}), .en(wr));  // open: in3
  Multiplexer multiplexer_3 (.in0(1'b0), .in1(not_1_out), .out(LWR), .sel(ByteEn));
  not not_1 (not_1_out, A0);
  Multiplexer #(.select(2), .width(16)) multiplexer_4 (
    .in0(dataIn), .in1(and_1_out), .in2(shifter_1_out), .out(dout), .sel({LWR, HWR}));  // open: in3
endmodule
